# Fritzing sketch wiring (saved by Fritzing 0.9.3b)

parts:
  Часть1 = Arduino Mega 2560 (Rev3)
  M1 = DC Motor  # not connected
  M2 = DC Motor  # not connected
  M3 = BTS7960
  M4 = BTS7960
  M5 = ps2 gamepad [package=THT]
  Часть3 = Mini560 buck module
  Часть4 = OLED Monochrome 128x64 0.96 inch [part_number=326]
  U1 = WS2812 RGB LED strip
  BAT1 = 12 battery [package=battery]  # not connected

nets:
  N1: Часть1.D21/SCL, Часть4.SCLK_SCK
  N2: Часть1.D20/SDA, Часть4.MOSI_SDA
  GND: Часть1.GND, M3.pin8, M4.pin8, M5.GND, Часть3.GND2*
  N3: Часть1.D12_PWM, U1.DIN
  N4: Часть1.D11_PWM, M5.CMD
  N5: Часть1.D10_PWM, M5.ATT
  N6: Часть1.D9_PWM, M3.pin1
  N7: Часть1.D8_PWM, M3.pin2
  3V3: Часть1.3V3, M5.3.3V
  N8: Часть1.VIN, Часть3.Vout1
  N9: Часть1.D3_PWM, M4.pin2
  N10: Часть1.D5_PWM, M4.pin1
  N11: Часть1.D30, M5.DAT
  N12: Часть1.D31, M5.CLK
  N13: M3.pin3, M3.pin4, M3.pin7
  N14: M4.pin3, M4.pin4, M4.pin7

custom parts:
  BTS7960: BTS7960 43A Peak Power H-Bridge PWM Motor Driver
  ps2 gamepad: PS2 gamepad. Warning! PCB view is designed for the female connector available from https://www.robotshop.com/en/ps2-connector.html. However there is no mechanical information that I can find so ipcb was generated from a scaled jpg and may well be wrong. Print the footprint out and check it against a real part before ordering boards!
  Mini560 buck module: DC-DC Power module Input: DC 5.5~20V; Output: 3.3V (+/-0.05V error)
  OLED Monochrome 128x64 0.96 inch: These displays are small, only about 1" diameter, but very readable due to the high contrast of an OLED display. This display is made of 128x64 individual white OLED pixels, each one is turned on or off by the controller chip. Because the display makes its own light, no backlight is required. This reduces the power required to run the OLED and is why the display has such high contrast; we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
  WS2812 RGB LED strip: WS2812 strip
  12 battery: 12V lead acid type battery, like the Husqvarna YTH2448 12V 35AH battery. The pads in pcb are sized to accomidate up to 14ga wire (as these batterys will deliver high currents.)
